# Fritzing sketch mainboard (saved by Fritzing 0.9.2b)
perfboards: 1

parts:
  Bauteil1 = Arduino Micro (Rev3)
  J1 = female pin header, 2 pins [form="♀ (female)"]
  J2 = female pin header, 2 pins [form="♀ (female)"]
  J3 = female pin header, 2 pins [form="♀ (female)"]
  J6 = female pin header, 2 pins [form="♀ (female)"]
  R1 = Resistor [tolerance=±5% resistance=10k package=THT]
  R2 = Resistor [tolerance=±5% resistance=10k package=THT]
  R3 = Resistor [tolerance=±5% resistance=10k package=THT]
  R4 = Resistor [tolerance=±5% resistance=10k package=THT]
  R5 = Resistor [tolerance=±5% resistance=10k package=THT]
  R6 = Resistor [tolerance=±5% resistance=10k package=THT]
  J7 = female pin header, 2 pins [form="♀ (female)"]
  R7 = Resistor [tolerance=±5% resistance=10k package=THT]
  J4 = female pin header, 2 pins [form="♀ (female)"]
  J5 = female pin header, 2 pins [form="♀ (female)"]
  J8 = female pin header, 2 pins [form="♀ (female)"]
  R8 = Resistor [tolerance=±5% resistance=10k package=THT]
  R9 = Resistor [tolerance=±5% resistance=10k package=THT]
  R10 = Resistor [tolerance=±5% resistance=10k package=THT]
  R11 = Resistor [tolerance=±5% resistance=10k package=THT]
  R12 = Resistor [tolerance=±5% resistance=10k package=THT]
  R13 = Resistor [tolerance=±5% resistance=10k package=THT]
  R14 = Resistor [tolerance=±5% resistance=10k package=THT]
  R15 = Resistor [tolerance=±5% resistance=10k package=THT]
  R16 = Resistor [tolerance=±5% resistance=10k package=THT]
  R17 = Resistor [tolerance=±5% resistance=10k package=THT]
  R18 = Resistor [tolerance=±5% resistance=10k package=THT]
  J9 = female pin header, 2 pins [form="♀ (female)"]
  J10 = female pin header, 2 pins [form="♀ (female)"]
  J11 = female pin header, 2 pins [form="♀ (female)"]
  J12 = female pin header, 2 pins [form="♀ (female)"]
  J13 = female pin header, 2 pins [form="♀ (female)"]
  J14 = female pin header, 2 pins [form="♀ (female)"]
  J15 = female pin header, 2 pins [form="♀ (female)"]
  J16 = female pin header, 2 pins [form="♀ (female)"]
  J17 = female pin header, 2 pins [form="♀ (female)"]
  J18 = female pin header, 2 pins [form="♀ (female)"]
  J19 = female pin header, 2 pins [form="♀ (female)"]
  J20 = female pin header, 2 pins [form="♀ (female)"]
  R19 = Resistor [tolerance=±5% resistance=10k package=THT]
  R20 = Resistor [tolerance=±5% resistance=10k package=THT]
  R21 = Resistor [tolerance=±5% resistance=150 package=THT]
  J21 = female pin header, 2 pins [form="♀ (female)"]

nets:
  N1: Bauteil1.D1/TX, J20.pin1, R20.Pin_0
  N2: Bauteil1.D0/RX, J19.pin1, R19.Pin_0
  N3: Bauteil1.GND, R1.Pin_0, R2.Pin_0, R3.Pin_0, R4.Pin_0, R5.Pin_0, R6.Pin_0, R7.Pin_0, R8.Pin_1, R9.Pin_1, R10.Pin_1, R11.Pin_1, R12.Pin_1, R13.Pin_1, R14.Pin_1, R15.Pin_1, R16.Pin_1, R17.Pin_1, R18.Pin_1, R19.Pin_1, R20.Pin_1
  N4: Bauteil1.D2/SDA, R18.Pin_0, J18.pin1
  N5: Bauteil1.D3/SCL, R17.Pin_0, J17.pin1
  N6: Bauteil1.D4_PWM/A6, R16.Pin_0, J16.pin1
  N7: Bauteil1.D5_PWM, R15.Pin_0, J15.pin1
  N8: Bauteil1.D6_PWM/A7, R14.Pin_0, J14.pin1
  N9: Bauteil1.D7, R13.Pin_0, J13.pin1
  N10: Bauteil1.D8_PWM/A8, R12.Pin_0, J12.pin1
  N11: Bauteil1.D9_PWM/A9, R11.Pin_0, J11.pin1
  N12: Bauteil1.D10_PWM/A10, R10.Pin_0, J10.pin1
  N13: Bauteil1.D11_PWM, R9.Pin_0, J9.pin1
  N14: Bauteil1.D12_PWM/A11, J8.pin1, R8.Pin_0
  N15: Bauteil1.5V, J1.pin2, J2.pin2, J3.pin2, J6.pin2, J7.pin2, J4.pin2, J5.pin2, J8.pin2, J9.pin2, J10.pin2, J11.pin2, J12.pin2, J13.pin2, J14.pin2, J15.pin2, J16.pin2, J17.pin2, J18.pin2, J19.pin2, J20.pin2, J21.pin1
  N16: Bauteil1.A5, J6.pin1, R1.Pin_1
  N17: Bauteil1.A4, R2.Pin_1, J5.pin1
  N18: Bauteil1.A3, R3.Pin_1, J4.pin1
  N19: Bauteil1.A2, J3.pin1, R4.Pin_1
  N20: Bauteil1.A1, J2.pin1, R5.Pin_1
  N21: Bauteil1.A0, J1.pin1, R6.Pin_1
  N22: Bauteil1.D13_PWM, J7.pin1, R7.Pin_1
  N23: R21.Pin_1, J21.pin2
